# Fritzing sketch Voltmeter SD RTC FDTI Breakout (saved by Fritzing 0.8.7b)
breadboards: 1

parts:
  Part1 = Arduino Pro Mini v13
  Part2 = FTDI Basic Programmer
  ZS-042_RTC1 = ZS-042 RTC Module
  Part3 = MicroSD Card Module
  U1 = BATTERY-2 [package=battery-aa]

nets:
  N1: Part1.DTR, Part2.DTR
  N2: Part1.D0/TX, Part2.RXI
  N3: Part1.D1/RX, Part2.TXO
  VCC: Part1.VCC, Part2.POWER, ZS-042_RTC1.VCC, Part3.VCC
  GND: Part1.GND, Part2.CTS, Part2.GND, ZS-042_RTC1.GND, Part3.GND, U1.+1
  N4: Part1.A4, ZS-042_RTC1.SDA
  N5: Part1.A5, ZS-042_RTC1.SCL
  N6: Part1.A0, U1.-1
  N7: Part1.D13/SCK, Part3.SCK
  N8: Part1.D12/MISO, Part3.MISO
  N9: Part1.D11_PWM/MOSI, Part3.MOSI
  N10: Part1.D10_PWM/SS, Part3.CS
  N11: Part1.D2, ZS-042_RTC1.SQW

notes:
  The AA battery represents an example of what you can take the voltage of...
