# Fritzing sketch Voltmeter SD RTC LiPo Connected (saved by Fritzing 0.8.7b)
breadboards: 1

parts:
  Part1 = Arduino Pro Mini v13
  ZS-042_RTC1 = ZS-042 RTC Module
  Part3 = MicroSD Card Module
  U1 = BATTERY-2 [package=battery-aa]
  U2 = LIPO-2000mAh [package=lipo-2000]

nets:
  N1: Part1.A4, ZS-042_RTC1.SDA
  N2: Part1.A5, ZS-042_RTC1.SCL
  N3: Part1.RAW, U2.+
  GND: Part1.GND, ZS-042_RTC1.GND, Part3.GND, U1.+1, U2.-
  VCC: Part1.VCC, ZS-042_RTC1.VCC, Part3.VCC
  N4: Part1.A0, U1.-1
  N5: Part1.D13/SCK, Part3.SCK
  N6: Part1.D12/MISO, Part3.MISO
  N7: Part1.D11_PWM/MOSI, Part3.MOSI
  N8: Part1.D10_PWM/SS, Part3.CS
  N9: Part1.D2, ZS-042_RTC1.SQW

notes:
  The AA Battery is an example of how to test voltage
